# Fritzing sketch Tacitus B0 (Bluetooth) (saved by Fritzing 0.8.7b)
circuit board: 5.6cm x 3.3cm
breadboards: 1

parts:
  BATT1 = LiPoly Battery (1300mAh)
  M1 = DC Motor
  M2 = DC Motor
  Teensy_3_1 = Teensy 3.1
  US1 = HC-SR04 [package=THT]
  U2 = BLUETOOTH-RN41 [package=rn41]  # not connected
  Q3 = MOSFET-NCHANNEL [package=sot23-3]  # not connected
  IMU1 = GY-521

nets:
  VCC: BATT1.positive, M1.pin_1, M2.pin_1, Teensy_3_1.Vin, US1.VCC, IMU1.VCC
  GND: BATT1.negative, Teensy_3_1.GND, US1.GND, IMU1.GND
  N1: Teensy_3_1.D7, US1.Echo
  N2: Teensy_3_1.D8, US1.Trig
  N3: Teensy_3_1.A3/D17, IMU1.INT
  N4: Teensy_3_1.A4/D18, IMU1.SDA
  N5: Teensy_3_1.A5/D19, IMU1.SCL

custom parts:
  LiPoly Battery (1300mAh): Lithium Ion Polymer Battery (1300mAh)
  HC-SR04: The HC-SR04 Ultrasonic Sensor. Provides millimeter accurate sonar distance measurement out to 3-5 meters, and can scan reliably up to 50 times per second.
  GY-521: Description: This breakout board incorporates the MPU-6050 from Invensense and provides the necessary power delivery (through level shifter) and I2C pins. Has 6DOF from an accel + gyro setup.
