# Fritzing sketch Tacitus C0 (saved by Fritzing 0.8.7b)
breadboards: 1

parts:
  U1 = ATmega328 [package=tqfp]
  Y1 = Resonator [frequency="16 Mhz" package=THT]
  R1 = Resistor [tolerance=±5% resistance=220 package="0805 [SMD]"]  # not connected
  LED1 = smd LED [color="Green (570nm)" package="0805 [SMD]"]  # not connected
  C1 = Ceramic Capacitor [capacitance=100nF package="0805 [SMD, multilayer]"]  # not connected
  Q1 = MOSFET-NCHANNEL [package=sot23-3]  # not connected
  V1 = DC Power [voltage=5]
  IC1 = Voltage Regulator [package=sot23-5]
  C2 = Ceramic Capacitor [capacitance=10µF voltage=10V package="0805 [SMD, multilayer]"]
  C3 = Ceramic Capacitor [capacitance=10µF voltage=10V package="0805 [SMD, multilayer]"]
  J1 = AVR ISP 6 Pin [package=2x3-ns]

nets:
  GND: U1.GND, U1.AGND, Y1.GND, V1.V-, IC1.GND, C2.0, C3.0, J1.6
  5V: U1.VCC, U1.AVCC, U1.AREF, IC1.OUT, C3.1
  N1: U1.PB6(XTAL1_TOSC1), Y1.0
  N2: U1.PB7(XTAL2_TOSC2), Y1.pin_1
  N3: V1.V+, IC1.IN, IC1.EN, C2.1
