# Fritzing sketch TacitusARM (saved by Fritzing 0.8.7b)
circuit board: 5cm x 3.65cm
breadboards: 1

parts:
  BATT1 = LiPoly Battery (1300mAh)
  IMU1 = GY-521
  Q1 = NPN-Transistor [package="TO92 [THT]"]
  Q2 = NPN-Transistor [package="TO92 [THT]"]
  M1 = DC Motor
  M2 = DC Motor
  Teensy_3_1 = Teensy 3.1
  US1 = HC-SR04 [package=THT]

nets:
  VCC: BATT1.positive, IMU1.VCC, M1.pin_1, M2.pin_1, Teensy_3_1.Vin, US1.VCC
  GND: BATT1.negative, IMU1.GND, Q1.E, Q2.E, Teensy_3_1.GND, US1.GND
  N1: IMU1.SCL, Teensy_3_1.A5/D19
  N2: IMU1.SDA, Teensy_3_1.A4/D18
  N3: IMU1.INT, Teensy_3_1.A3/D17
  N4: Q1.B, Teensy_3_1.A2/D16
  N5: Q1.C, M1.pin_2
  N6: Q2.B, Teensy_3_1.A1/D15
  N7: Q2.C, M2.pin_2
  N8: Teensy_3_1.D7, US1.Echo
  N9: Teensy_3_1.D8, US1.Trig

notes:
  Trig=8 Echo=7

custom parts:
  LiPoly Battery (1300mAh): Lithium Ion Polymer Battery (1300mAh)
  GY-521: Description: This breakout board incorporates the MPU-6050 from Invensense and provides the necessary power delivery (through level shifter) and I2C pins. Has 6DOF from an accel + gyro setup.
  HC-SR04: The HC-SR04 Ultrasonic Sensor. Provides millimeter accurate sonar distance measurement out to 3-5 meters, and can scan reliably up to 50 times per second.
