# Fritzing sketch bareduino (saved by Fritzing 0.8.7b)
circuit board: 2.5cm x 2.4cm
breadboards: 1

parts:
  U1 = ATmega328 [package=tqfp]
  J3 = AVR ISP 6 Pin [package=2x3_offset]
  J4 = longpad pin header, 3 pins [form="long pad"]
  Pad1 = Pad [width=1.6 height=2 connect=center]
  Pad2 = Pad [width=1.6 height=2 connect=center]

nets:
  N1: U1.VCC, J3.2
  GND: U1.AGND, J3.6, J4.pin2
  N2: U1.PB6(XTAL1_TOSC1), J4.pin3
  N3: U1.PB7(XTAL2_TOSC2), J4.pin1
  N4: U1.PB3(MOSI_OC2), J3.4
  N5: U1.PB4(MISO), J3.1
  N6: U1.PB5(SCK), J3.3
  N7: U1.PC6(_RESET), J3.5, Pad1.pad, Pad2.pad
